# Fritzing sketch BD20 (saved by Fritzing 0.9.6b)
circuit board: 8.46667cm x 5.64444cm
breadboards: 1

parts:
  D1 = Rectifier Diode [part_number=1N4001 package="300 mil [THT]"]
  D2 = Rectifier Diode [part_number=1N4001 package="300 mil [THT]"]
  D3 = Rectifier Diode [part_number=1N4001 package="300 mil [THT]"]
  L1 = Inductor [package="400 mil [THT]"]
  J1 = screw terminal, 4 pins
  Q1 = NPN-Transistor [package="TO92 [THT]"]
  C1 = Tantalum Capacitor [capacitance=1μF voltage=35V package="100 mil [THT, tantalum]"]
  R1 = Resistor [tolerance=±5% power=0.25 resistance=470 package=THT]
  Q2 = Basic FET N-Channel [package="TO220 [THT]"]  # not connected
  R2 = Resistor [tolerance=±5% power=0.25 resistance=47k package=THT]
  R3 = Resistor [tolerance=±5% power=0.25 resistance=1.5k package=THT]
  D4 = Rectifier Diode [part_number=1N4001 package="300 mil [THT]"]
  R4 = Resistor [tolerance=±5% power=0.25 resistance=47 package=THT]

nets:
  N1: D1.cathode, D3.anode
  N2: D1.anode, D2.cathode, L1.pin_0, R1.Pin_0
  N3: D2.anode, D3.cathode
  N4: L1.pin_1, J1.pin4, Q1.E, C1.-
  N5: J1.pin1, D4.anode
  N6: J1.pin2, R4.Pin_1
  N7: J1.pin3, Q1.C, C1.+, R2.Pin_1
  N8: Q1.B, R1.Pin_1
  N9: R2.Pin_0, R3.Pin_1
  N10: R3.Pin_0, D4.cathode
