# Fritzing sketch NCE_BD20 (saved by Fritzing 0.9.6b)
breadboards: 1

parts:
  Q1 = NPN-Transistor [package="TO92 [THT]"]
  J1 = Camdenboss CTB0158-4 [part_number=CTB0158-4 package=THT]
  C1 = Tantalum Capacitor [capacitance=1μF voltage=35V package="100 mil [THT, tantalum]"]
  R1 = Resistor [tolerance=±5% power=0.25 resistance=47k package=THT]
  R2 = Resistor [tolerance=±5% power=0.25 resistance=1.8k package=THT]
  D1 = Rectifier Diode [part_number=1N4001 package="300 mil [THT]"]
  R3 = Resistor [tolerance=±5% power=0.25 resistance=10k package=THT]
  R4 = Resistor [tolerance=±5% power=0.25 resistance=1.8k package=THT]
  LED1 = LED - 5mm [color="Red (633nm)" current=0.030 package="5 mm [THT]"]
  R5 = Resistor [tolerance=±5% power=0.25 resistance=47 package=THT]
  R6 = Resistor [tolerance=±5% power=0.25 resistance=470k package=THT]
  L1 = Inductor [package="400 mil [THT]"]
  D3 = Rectifier Diode [part_number=1N4001 package="300 mil [THT]"]
  D4 = Rectifier Diode [part_number=1N4001 package="300 mil [THT]"]
  D5 = Rectifier Diode [part_number=1N4001 package="300 mil [THT]"]
  R7 = Trimmer Potentiometer [maximum_resistance=5kΩ package=THT]
  R9 = Resistor [tolerance=±5% power=0.25 resistance=2.2k package=THT]
  IO1 = PCF8574N [package="DIP16 [THT]"]
  D2 = Zener Diode [part_number=1N4732A breakdown_voltage=5.1V package="300 mil [THT]"]
  Q4 = Basic FET N-Channel [package="TO220 [THT]"]
  Q5 = Basic FET N-Channel [package="TO220 [THT]"]
  Q6 = NPN-Transistor [package="TO92 [THT]"]
  R10 = Resistor [tolerance=±5% power=0.25 resistance=2.7k package=THT]
  R11 = Resistor [tolerance=±5% power=0.25 resistance=7.2k package=THT]
  Q7 = NPN-Transistor [package="TO92 [THT]"]
  R12 = Resistor [tolerance=±5% power=0.25 resistance=3k package=THT]

nets:
  N1: Q1.E, J1.pin1, C1.-, L1.pin_1, D4.anode, D5.cathode, R7.leg1, R7.wiper, D2.anode, Q4.source, Q5.source
  N2: Q1.B, R6.Pin_1
  N3: Q1.C, J1.pin2, C1.+, R1.Pin_1, Q5.gate
  N4: J1.pin3, R5.Pin_1
  N5: J1.pin4, D1.anode
  N6: J1.terminal_1, IO1.GND, Q7.E, R12.Pin_1
  N7: J1.terminal_3, R10.Pin_0
  N8: R1.Pin_0, R2.Pin_1, D2.cathode
  N9: R2.Pin_0, D1.cathode, R3.Pin_0, R4.Pin_0
  N10: R3.Pin_1, Q4.gate, Q5.drain
  N11: R4.Pin_1, LED1.anode
  N12: LED1.cathode, R5.Pin_0, Q4.drain
  N13: R6.Pin_0, L1.pin_0, D3.anode, D4.cathode, R7.leg2
  N14: D3.cathode, D5.anode
  3.3V: R9.Pin_0
  N15: R9.Pin_1, IO1.P0, Q6.C, Q7.C
  N16: Q6.E, R11.Pin_1, Q7.B, R12.Pin_0
  N17: Q6.B, R10.Pin_1, R11.Pin_0

notes:
  GND
  Logic
  Relay
  +5V
  NCE BD20

custom parts:
  PCF8574N: Remote 8-Bit I/O Expander for I 2C Bus
