# Fritzing sketch BlockDetection_InputDriver (saved by Fritzing 0.9.6b)
stripboards: 1

parts:
  J1 = female pin header, 40 pins [form="♀ (female)" part_number="40 PIN Single Row Right Angle FEMALE PIN HEADER 2.54MM"]
  IO1 = ULN2803A [form="♂ (male)" part_number=ULN2803A package=THT]
  IO2 = ULN2803A [form="♂ (male)" part_number=ULN2803A package=THT]
  IO3 = ULN2803A [form="♂ (male)" part_number=ULN2803A package=THT]
  IO4 = ULN2803A [form="♂ (male)" part_number=ULN2803A package=THT]
  J3 = screw terminal, 9 pins [part_number="KF128 2.54mm "]
  J4 = screw terminal, 9 pins [part_number="KF128 2.54mm "]
  J5 = screw terminal, 9 pins [part_number="KF128 2.54mm "]
  J6 = screw terminal, 9 pins [part_number="KF128 2.54mm "]

nets:
  N1: J1.pin2, IO4.pin9, J3.pin9
  N2: J1.pin3, IO4.pin11
  N3: J1.pin4, IO4.pin12
  N4: J1.pin5, IO4.pin13
  N5: J1.pin6, IO4.pin14
  N6: J1.pin7, IO4.pin15
  N7: J1.pin8, IO4.pin16
  N8: J1.pin9, IO4.pin17
  N9: J1.pin10, IO4.pin18
  N10: J1.pin12, IO3.pin9, J4.pin9
  N11: J1.pin13, IO3.pin11
  N12: J1.pin14, IO3.pin12
  N13: J1.pin15, IO3.pin13
  N14: J1.pin16, IO3.pin14
  N15: J1.pin17, IO3.pin15
  N16: J1.pin18, IO3.pin16
  N17: J1.pin19, IO3.pin17
  N18: J1.pin20, IO3.pin18
  N19: J1.pin22, IO2.pin9, J5.pin9
  N20: J1.pin23, IO2.pin11
  N21: J1.pin24, IO2.pin12
  N22: J1.pin25, IO2.pin13
  N23: J1.pin26, IO2.pin14
  N24: J1.pin27, IO2.pin15
  N25: J1.pin28, IO2.pin16
  N26: J1.pin29, IO2.pin17
  N27: J1.pin30, IO2.pin18
  N28: J1.pin32, IO1.pin9, J6.pin9
  N29: J1.pin33, IO1.pin11
  N30: J1.pin34, IO1.pin12
  N31: J1.pin35, IO1.pin13
  N32: J1.pin36, IO1.pin14
  N33: J1.pin37, IO1.pin15
  N34: J1.pin38, IO1.pin16
  N35: J1.pin39, IO1.pin17
  N36: J1.pin40, IO1.pin18
  N37: IO1.pin1, J6.pin1
  N38: IO1.pin2, J6.pin2
  N39: IO1.pin3, J6.pin3
  N40: IO1.pin4, J6.pin4
  N41: IO1.pin5, J6.pin5
  N42: IO1.pin6, J6.pin6
  N43: IO1.pin7, J6.pin7
  N44: IO1.pin8, J6.pin8
  N45: IO2.pin1, J5.pin1
  N46: IO2.pin2, J5.pin2
  N47: IO2.pin3, J5.pin3
  N48: IO2.pin4, J5.pin4
  N49: IO2.pin5, J5.pin5
  N50: IO2.pin6, J5.pin6
  N51: IO2.pin7, J5.pin7
  N52: IO2.pin8, J5.pin8
  N53: IO3.pin1, J4.pin1
  N54: IO3.pin2, J4.pin2
  N55: IO3.pin3, J4.pin3
  N56: IO3.pin4, J4.pin4
  N57: IO3.pin5, J4.pin5
  N58: IO3.pin6, J4.pin6
  N59: IO3.pin7, J4.pin7
  N60: IO3.pin8, J4.pin8
  N61: IO4.pin1, J3.pin1
  N62: IO4.pin2, J3.pin2
  N63: IO4.pin3, J3.pin3
  N64: IO4.pin4, J3.pin4
  N65: IO4.pin5, J3.pin5
  N66: IO4.pin6, J3.pin6
  N67: IO4.pin7, J3.pin7
  N68: IO4.pin8, J3.pin8

notes:
  Output pins til I2C I/O Interface
  Input pins fra NCE-BD20

custom parts:
  ULN2803A: Generic male header
