# Fritzing sketch CurrentLoop (saved by Fritzing 0.9.6b)
breadboards: 1

parts:
  D1 = Rectifier Diode [part_number=1N4001 package="300 mil [THT]"]
  D2 = Rectifier Diode [part_number=1N4001 package="300 mil [THT]"]
  Q1 = PNP-Transistor [package="TO92 [THT]"]
  J1 = female pin header, 3 pins [form="♀ (female)"]
  U1 = TLP620 [package="DIP (Dual Inline) [THT]"]
  R1 = Resistor [tolerance=±5% power=0.25 resistance=220 package=THT]
  M1 = DOIT Esp32 DevKit v1 (30 pins long, 11 pins width) [part_number="ESP32 with adc"]
  R2 = Resistor [tolerance=±5% power=0.25 resistance=220 package=THT]
  R3 = Resistor [tolerance=±5% power=0.25 resistance=220 package=THT]
  R4 = Resistor [tolerance=±5% power=0.25 resistance=220 package=THT]

nets:
  N1: D1.cathode, D2.anode, Q1.B, J1.pin2
  N2: D1.anode, D2.cathode, Q1.E, J1.pin1
  N3: Q1.C, U1.pin1
  N4: J1.pin3, R1.Pin_0
  N5: U1.pin2, R1.Pin_1
  N6: U1.pin3, M1.D5, R3.Pin_1, R4.Pin_0
  N7: U1.pin4, R2.Pin_0, R3.Pin_0
  N8: M1.3V3, R2.Pin_1
  GND: M1.GND, R4.Pin_1
  5V: M1.VIN

notes:
  4-10 mA loop
  ADC
  DCC
  Track
  Gnd

custom parts:
  TLP620: Photo-transistor optically coupled to two infrared emitting diodes connected in inverse parallel.
  DOIT Esp32 DevKit v1 (30 pins long, 11 pins width): The DOIT Esp32 DevKit v1 is one of the development board created by DOIT to evaluate the ESP-WROOM-32 module. It is based on the ESP32 microcontroller that boasts Wifi, Bluetooth, Ethernet and Low Power support all in a single chip. (vanepp) made breadboard work, adjusted pin numbering and labels and reduced size of schematic and cleaned up pcb. This chip is 30pins long (2 x15) and 11 pins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
