# Fritzing sketch DCC Block Detect BC557B (saved by Fritzing 0.9.6b)
circuit board: 10cm x 5cm
breadboards: 1

parts:
  BC557B = PNP-Transistor [package="TO92 [THT]"]
  D1 = Rectifier Diode [part_number=1N4001 package="300 mil [THT]"]
  D2 = Rectifier Diode [part_number=1N4001 package="300 mil [THT]"]
  IO1 = ULN2803A [form="♂ (male)" part_number=ULN2803A package=THT]
  UEXT_ESP32-Poe-ISO = shrouded pin header, 10 pins [form="♂ (shrouded male)"]
  R1 = 8 Resistor Network [part_number=10k package="SIP (Single Inline)"]
  J1 = screw terminal, 9 pins

nets:
  N1: BC557B.E, D1.anode, D2.cathode, J1.pin1
  N2: BC557B.B, D1.cathode, D2.anode, J1.pin2
  N3: BC557B.C, IO1.pin1
  GND: IO1.pin9, UEXT_ESP32-Poe-ISO.pin10
  3v3: IO1.pin10, UEXT_ESP32-Poe-ISO.pin1, R1.1
  GPIO36: IO1.pin11, UEXT_ESP32-Poe-ISO.pin9, R1.2
  GPIO13: IO1.pin12, UEXT_ESP32-Poe-ISO.pin8, R1.3
  GPIO2: IO1.pin13, UEXT_ESP32-Poe-ISO.pin7, R1.4
  GPIO5: IO1.pin14, UEXT_ESP32-Poe-ISO.pin6, R1.5
  GPIO14: IO1.pin15, UEXT_ESP32-Poe-ISO.pin5, R1.6
  GPIO15: IO1.pin16, UEXT_ESP32-Poe-ISO.pin4, R1.7
  GPIO16: IO1.pin17, UEXT_ESP32-Poe-ISO.pin3, R1.8
  GPIO4: IO1.pin18, UEXT_ESP32-Poe-ISO.pin2, R1.9

notes:
  Power
  Track1
  Track2
  Track3
  Track4
  Track5
  Track6
  Track7
  Track8

custom parts:
  ULN2803A: Generic male header
