# Fritzing sketch DCC Block Detect module (saved by Fritzing 0.9.6b)
circuit board: 8.46667cm x 5.64444cm
breadboards: 1

parts:
  D2 = Rectifier Diode [part_number=1N4001 package="300 mil [THT]"]
  D3 = Rectifier Diode [part_number=1N4001 package="300 mil [THT]"]
  D4 = Rectifier Diode [part_number=1N4001 package="300 mil [THT]"]
  J2 = female pin header, 3 pins [form="♀ (female)"]
  R1 = Resistor [tolerance=±5% power=0.25 resistance=470 package=THT]
  J1 = female pin header, 2 pins [form="♀ (female)"]
  J3 = female pin header, 6 pins [form="♀ (female)"]
  C1 = Ceramic Capacitor [capacitance=0.47µF voltage=35V package="100 mil [THT, multilayer]"]
  Q1 = NPN-Transistor [package="TO92 [THT]"]

nets:
  N1: D2.cathode, D3.anode, J2.pin1, R1.Pin_0, J3.pin1
  N2: D2.anode, D4.cathode, J2.pin2, J2.pin3, J1.pin2, J3.pin6, C1.0, Q1.E
  N3: D3.cathode, D4.anode
  N4: R1.Pin_1, Q1.B
  N5: J1.pin1, C1.1, Q1.C
