# Fritzing sketch BD20_InputInterface_002 (saved by Fritzing 0.9.6b)
circuit board: 11cm x 3.15cm

parts:
  IO1 = ULN2803A [form="♂ (male)" part_number=ULN2803A package=THT]
  IO2 = ULN2803A [form="♂ (male)" part_number=ULN2803A package=THT]
  IO3 = ULN2803A [form="♂ (male)" part_number=ULN2803A package=THT]
  IO4 = ULN2803A [form="♂ (male)" part_number=ULN2803A package=THT]
  J5 = screw terminal, 9 pins [part_number="KF128 2.54mm "]
  J4 = screw terminal, 9 pins [part_number="KF128 2.54mm "]
  J3 = screw terminal, 9 pins [part_number="KF128 2.54mm "]
  J2 = screw terminal, 9 pins [part_number="KF128 2.54mm "]
  J6 = screw terminal, 9 pins [part_number="KF128 2.54mm "]
  J7 = screw terminal, 9 pins [part_number="KF128 2.54mm "]
  J8 = screw terminal, 9 pins [part_number="KF128 2.54mm "]
  J9 = screw terminal, 9 pins [part_number="KF128 2.54mm "]
  J1 = female pin header, 40 pins [form="♀ (female)" part_number="40 PIN Single Row Right Angle FEMALE PIN HEADER 2.54MM"]

nets:
  N1: IO1.pin1, J2.pin9, J6.pin9
  N2: IO1.pin2, J2.pin8, J6.pin8
  N3: IO1.pin3, J2.pin7, J6.pin7
  N4: IO1.pin4, J2.pin6, J6.pin6
  N5: IO1.pin5, J2.pin5, J6.pin5
  N6: IO1.pin6, J2.pin4, J6.pin4
  N7: IO1.pin7, J2.pin3, J6.pin3
  N8: IO1.pin8, J2.pin2, J6.pin2
  GND: IO1.pin9, IO2.pin9, IO3.pin9, IO4.pin9, J5.pin1, J4.pin1, J3.pin1, J2.pin1, J6.pin1, J7.pin1, J8.pin1, J9.pin1, J1.pin10, J1.pin20, J1.pin30, J1.pin40
  3V3: IO1.pin10, IO2.pin10, IO3.pin10, IO4.pin10, J1.pin1
  N9: IO1.pin11, J1.pin9
  N10: IO1.pin12, J1.pin8
  N11: IO1.pin13, J1.pin7
  N12: IO1.pin14, J1.pin6
  N13: IO1.pin15, J1.pin5
  N14: IO1.pin16, J1.pin4
  N15: IO1.pin17, J1.pin3
  N16: IO1.pin18, J1.pin2
  N17: IO2.pin1, J3.pin9, J7.pin9
  N18: IO2.pin2, J3.pin8, J7.pin8
  N19: IO2.pin3, J3.pin7, J7.pin7
  N20: IO2.pin4, J3.pin6, J7.pin6
  N21: IO2.pin5, J3.pin5, J7.pin5
  N22: IO2.pin6, J3.pin4, J7.pin4
  N23: IO2.pin7, J3.pin3, J7.pin3
  N24: IO2.pin8, J3.pin2, J7.pin2
  N25: IO2.pin11, J1.pin19
  N26: IO2.pin12, J1.pin18
  N27: IO2.pin13, J1.pin17
  N28: IO2.pin14, J1.pin16
  N29: IO2.pin15, J1.pin15
  N30: IO2.pin16, J1.pin14
  N31: IO2.pin17, J1.pin13
  N32: IO2.pin18, J1.pin12
  N33: IO3.pin1, J4.pin9, J8.pin9
  N34: IO3.pin2, J4.pin8, J8.pin8
  N35: IO3.pin3, J4.pin7, J8.pin7
  N36: IO3.pin4, J4.pin6, J8.pin6
  N37: IO3.pin5, J4.pin5, J8.pin5
  N38: IO3.pin6, J4.pin4, J8.pin4
  N39: IO3.pin7, J4.pin3, J8.pin3
  N40: IO3.pin8, J4.pin2, J8.pin2
  N41: IO3.pin11, J1.pin29
  N42: IO3.pin12, J1.pin28
  N43: IO3.pin13, J1.pin27
  N44: IO3.pin14, J1.pin26
  N45: IO3.pin15, J1.pin25
  N46: IO3.pin16, J1.pin24
  N47: IO3.pin17, J1.pin23
  N48: IO3.pin18, J1.pin22
  N49: IO4.pin1, J5.pin9, J9.pin9
  N50: IO4.pin2, J5.pin8, J9.pin8
  N51: IO4.pin3, J5.pin7, J9.pin7
  N52: IO4.pin4, J5.pin6, J9.pin6
  N53: IO4.pin5, J5.pin5, J9.pin5
  N54: IO4.pin6, J5.pin4, J9.pin4
  N55: IO4.pin7, J5.pin3, J9.pin3
  N56: IO4.pin8, J5.pin2, J9.pin2
  N57: IO4.pin11, J1.pin39
  N58: IO4.pin12, J1.pin38
  N59: IO4.pin13, J1.pin37
  N60: IO4.pin14, J1.pin36
  N61: IO4.pin15, J1.pin35
  N62: IO4.pin16, J1.pin34
  N63: IO4.pin17, J1.pin33
  N64: IO4.pin18, J1.pin32

notes:
  Output pins til I2C I/O Interface
  Input pins fra NCE-BD20
  3V3
  BlockDetection_InputDriver_002
  20240815 1719
  0
  7
  1
  2
  3
  4
  5
  6
  A
  9
  C
  B
  E
  D
  8
  F
  Gn
  sekt1953@gmail.com

custom parts:
  ULN2803A: Generic male header
