# Fritzing sketch Sporbesat_001 (saved by Fritzing 0.9.6b)
stripboards: 1

parts:
  IO1 = ULN2803A [form="♂ (male)" part_number=ULN2804A package=THT]
  R1 = 8 Resistor Network [part_number=10K package="SIP (Single Inline)"]
  NPU = male pin header, 10 pins [form="♂ (male)"]
  D1 = Rectifier Diode [part_number=1N5402 package="300 mil [THT]"]
  D2 = Rectifier Diode [part_number=1N5402 package="300 mil [THT]"]
  Q1 = PNP-Transistor [part_number=BC557 package="TO92 [THT]"]
  J1 = male pin header, 1 pin [form="♂ (male)"]
  J2 = male pin header, 1 pin [form="♂ (male)"]
  R2 = Resistor [tolerance=±5% power=0.25 resistance=6.8k package=THT]
  D3 = Rectifier Diode [part_number=1N5402 package="300 mil [THT]"]
  D4 = Rectifier Diode [part_number=1N5402 package="300 mil [THT]"]
  Q2 = PNP-Transistor [part_number=BC557 package="TO92 [THT]"]
  J3 = male pin header, 1 pin [form="♂ (male)"]
  J4 = male pin header, 1 pin [form="♂ (male)"]
  R3 = Resistor [tolerance=±5% power=0.25 resistance=6.8k package=THT]
  J5 = male pin header, 2 pins [form="♂ (male)"]
  J6 = male pin header, 8 pins [form="♂ (male)"]
  J7 = male pin header, 2 pins [form="♂ (male)"]
  D5 = Rectifier Diode [part_number=1N5402 package="300 mil [THT]"]
  D6 = Rectifier Diode [part_number=1N5402 package="300 mil [THT]"]
  Q3 = PNP-Transistor [part_number=BC557 package="TO92 [THT]"]
  J8 = male pin header, 1 pin [form="♂ (male)"]
  J9 = male pin header, 1 pin [form="♂ (male)"]
  R4 = Resistor [tolerance=±5% power=0.25 resistance=6.8k package=THT]
  D7 = Rectifier Diode [part_number=1N5402 package="300 mil [THT]"]
  D8 = Rectifier Diode [part_number=1N5402 package="300 mil [THT]"]
  Q4 = PNP-Transistor [part_number=BC557 package="TO92 [THT]"]
  J10 = male pin header, 1 pin [form="♂ (male)"]
  J11 = male pin header, 1 pin [form="♂ (male)"]
  R5 = Resistor [tolerance=±5% power=0.25 resistance=6.8k package=THT]

nets:
  N1: IO1.pin1, J6.pin8
  N2: IO1.pin2, J6.pin7
  N3: IO1.pin3, J6.pin6
  N4: IO1.pin4, J6.pin5
  N5: IO1.pin5, J6.pin4
  N6: IO1.pin6, J6.pin3
  N7: IO1.pin7, J6.pin2
  N8: IO1.pin8, J6.pin1
  DCC Gnd: IO1.pin9, NPU.pin10, J5.pin2, J7.pin2
  VCC: IO1.pin10, R1.1, NPU.pin9, J7.pin1
  Besat-01: IO1.pin11, R1.2, NPU.pin8
  Besat-02: IO1.pin12, R1.3, NPU.pin7
  N9: IO1.pin13, R1.4, NPU.pin6
  N10: IO1.pin14, R1.5, NPU.pin5
  N11: IO1.pin15, R1.6, NPU.pin4
  N12: IO1.pin16, R1.7, NPU.pin3
  N13: IO1.pin17, R1.8, NPU.pin2
  N14: IO1.pin18, R1.9, NPU.pin1
  N15: D1.cathode, D2.anode, Q1.B, J1.pin1
  DCC In: D1.anode, D2.cathode, Q1.E, D3.anode, D4.cathode, Q2.E, J5.pin1, D5.anode, D6.cathode, Q3.E, D7.anode, D8.cathode, Q4.E
  N16: Q1.C, R2.Pin_1
  N17: J2.pin1, R2.Pin_0
  N18: D3.cathode, D4.anode, Q2.B, J3.pin1
  N19: Q2.C, R3.Pin_1
  N20: J4.pin1, R3.Pin_0
  N21: D5.cathode, D6.anode, Q3.B, J9.pin1
  N22: Q3.C, R4.Pin_1
  N23: J8.pin1, R4.Pin_0
  N24: D7.cathode, D8.anode, Q4.B, J10.pin1
  N25: Q4.C, R5.Pin_1
  N26: J11.pin1, R5.Pin_0

notes:
  DCC In
  DCC Gnd
  VCC
  GND

custom parts:
  ULN2803A: Generic male header
