# Fritzing sketch CPU_LightDriver (saved by Fritzing 0.9.6b)
stripboards: 1

parts:
  M1 = DOIT Esp32 DevKit v1 (30 pins long, 11 pins width) [part_number=ESP32S-PIN30]
  J1 = male pin header, 2 pins [form="♂ (male)"]
  J2 = male pin header, 6 pins [form="♂ (male)"]
  DC1 = HW-613 [package=THT]

nets:
  N1: M1.3V3, J2.pin2
  N2: M1.GND, J1.pin1, J2.pin6, DC1.pin2
  N3: M1.D21, J2.pin3
  N4: M1.D22, J2.pin4
  N5: M1.VIN, J2.pin1, DC1.pin1
  N6: J1.pin2, DC1.pin3

custom parts:
  DOIT Esp32 DevKit v1 (30 pins long, 11 pins width): The DOIT Esp32 DevKit v1 is one of the development board created by DOIT to evaluate the ESP-WROOM-32 module. It is based on the ESP32 microcontroller that boasts Wifi, Bluetooth, Ethernet and Low Power support all in a single chip. (vanepp) made breadboard work, adjusted pin numbering and labels and reduced size of schematic and cleaned up pcb. This chip is 30pins long (2 x15) and 11 pins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
  HW-613: DC-DC Converter, max 24V input
