# Fritzing sketch KF141R_001 (saved by Fritzing 0.9.6b)
circuit board: 11cm x 2.2cm

parts:
  J23 = female pin header, 40 pins [form="♀ (female)"]
  J24 = female pin header, 40 pins [form="♀ (female)"]
  J25 = female pin header, 40 pins [form="♀ (female)"]
  J22 = male pin header, 40 pins [form="♂ (male)"]

nets:
  GND: J23.pin1, J23.pin11, J23.pin21, J23.pin31, J24.pin1, J24.pin11, J24.pin21, J24.pin31, J25.pin1, J25.pin2, J25.pin3, J25.pin4, J25.pin5, J25.pin6, J25.pin7, J25.pin8, J25.pin9, J25.pin10, J25.pin11, J25.pin12, J25.pin13, J25.pin14, J25.pin15, J25.pin16, J25.pin17, J25.pin18, J25.pin19, J25.pin20, J25.pin21, J25.pin22, J25.pin23, J25.pin24, J25.pin25, J25.pin26, J25.pin27, J25.pin28, J25.pin29, J25.pin30, J25.pin31, J25.pin32, J25.pin33, J25.pin34, J25.pin35, J25.pin36, J25.pin37, J25.pin38, J25.pin39, J25.pin40, J22.pin1, J22.pin11, J22.pin21, J22.pin31
  N1: J23.pin2, J24.pin2, J22.pin2
  N2: J23.pin3, J24.pin3, J22.pin3
  N3: J23.pin4, J24.pin4, J22.pin4
  N4: J23.pin5, J24.pin5, J22.pin5
  N5: J23.pin6, J24.pin6, J22.pin6
  N6: J23.pin7, J24.pin7, J22.pin7
  N7: J23.pin8, J24.pin8, J22.pin8
  N8: J23.pin9, J24.pin9, J22.pin9
  Ext.: J23.pin10, J23.pin20, J24.pin10, J24.pin20, J22.pin10, J22.pin20
  N9: J23.pin12, J24.pin12, J22.pin12
  N10: J23.pin13, J24.pin13, J22.pin13
  N11: J23.pin14, J24.pin14, J22.pin14
  N12: J23.pin15, J24.pin15, J22.pin15
  N13: J23.pin16, J24.pin16, J22.pin16
  N14: J23.pin17, J24.pin17, J22.pin17
  N15: J23.pin18, J24.pin18, J22.pin18
  N16: J23.pin19, J24.pin19, J22.pin19
  N17: J23.pin22, J24.pin22, J22.pin22
  N18: J23.pin23, J24.pin23, J22.pin23
  N19: J23.pin24, J24.pin24, J22.pin24
  N20: J23.pin25, J24.pin25, J22.pin25
  N21: J23.pin26, J24.pin26, J22.pin26
  N22: J23.pin27, J24.pin27, J22.pin27
  N23: J23.pin28, J24.pin28, J22.pin28
  N24: J23.pin29, J24.pin29, J22.pin29
  12V: J23.pin30, J24.pin30, J22.pin30
  N25: J23.pin32, J24.pin32, J22.pin32
  N26: J23.pin33, J24.pin33, J22.pin33
  N27: J23.pin34, J24.pin34, J22.pin34
  N28: J23.pin35, J24.pin35, J22.pin35
  N29: J23.pin36, J24.pin36, J22.pin36
  N30: J23.pin37, J24.pin37, J22.pin37
  N31: J23.pin38, J24.pin38, J22.pin38
  N32: J23.pin39, J24.pin39, J22.pin39
  3V3: J23.pin40, J24.pin40, J22.pin40

notes:
  01
  02
  03
  04
  05
  06
  07
  08
  09
  10
  3V3
  GND
  12V
  11
  12
  EXT
  13
  14
  15
  16
  23
  24
  18
  17
  22
  19
  20
  21
  31
  32
  26
  25
  30
  27
  28
  29
  sekt1953@gmail.com
  20240908 2344
  OMJK
