# Fritzing sketch InputSimulator (saved by Fritzing 0.9.6b)
circuit board: 11cm x 2.2cm

parts:
  J1 = female pin header, 40 pins [form="♀ (female)" part_number="40 PIN Single Row Right Angle FEMALE PIN HEADER 2.54MM"]
  S1 = Pushbutton [package=THT]
  S2 = Pushbutton [package=THT]
  S3 = Pushbutton [package=THT]
  S4 = Pushbutton [package=THT]
  S5 = Pushbutton [package=THT]
  S6 = Pushbutton [package=THT]
  S7 = Pushbutton [package=THT]
  S8 = Pushbutton [package=THT]
  S9 = Pushbutton [package=THT]
  S10 = Pushbutton [package=THT]
  S15 = Pushbutton [package=THT]
  S13 = Pushbutton [package=THT]
  S11 = Pushbutton [package=THT]
  S16 = Pushbutton [package=THT]
  S14 = Pushbutton [package=THT]
  S12 = Pushbutton [package=THT]
  S20 = Pushbutton [package=THT]
  S19 = Pushbutton [package=THT]
  S23 = Pushbutton [package=THT]
  S21 = Pushbutton [package=THT]
  S22 = Pushbutton [package=THT]
  S17 = Pushbutton [package=THT]
  S24 = Pushbutton [package=THT]
  S18 = Pushbutton [package=THT]
  S28 = Pushbutton [package=THT]
  S27 = Pushbutton [package=THT]
  S31 = Pushbutton [package=THT]
  S29 = Pushbutton [package=THT]
  S30 = Pushbutton [package=THT]
  S25 = Pushbutton [package=THT]
  S32 = Pushbutton [package=THT]
  S26 = Pushbutton [package=THT]

nets:
  3V3: J1.pin1
  N1: J1.pin2, S1.leg1
  N2: J1.pin3, S2.leg1
  N3: J1.pin4, S3.leg1
  N4: J1.pin5, S4.leg1
  N5: J1.pin6, S5.leg1
  N6: J1.pin7, S6.leg1
  N7: J1.pin8, S7.leg1
  N8: J1.pin9, S8.leg1
  GND: J1.pin10, J1.pin20, J1.pin30, J1.pin40, S1.leg0, S2.leg0, S3.leg0, S4.leg0, S5.leg0, S6.leg0, S7.leg0, S8.leg0, S9.leg0, S10.leg0, S15.leg0, S13.leg0, S11.leg0, S16.leg0, S14.leg0, S12.leg0, S20.leg0, S19.leg0, S23.leg0, S21.leg0, S22.leg0, S17.leg0, S24.leg0, S18.leg0, S28.leg0, S27.leg0, S31.leg0, S29.leg0, S30.leg0, S25.leg0, S32.leg0, S26.leg0
  12V: J1.pin11
  N9: J1.pin12, S9.leg1
  N10: J1.pin13, S10.leg1
  N11: J1.pin14, S11.leg1
  N12: J1.pin15, S12.leg1
  N13: J1.pin16, S13.leg1
  N14: J1.pin17, S14.leg1
  N15: J1.pin18, S15.leg1
  N16: J1.pin19, S16.leg1
  EXT.: J1.pin21, J1.pin31
  N17: J1.pin22, S17.leg1
  N18: J1.pin23, S18.leg1
  N19: J1.pin24, S19.leg1
  N20: J1.pin25, S20.leg1
  N21: J1.pin26, S21.leg1
  N22: J1.pin27, S22.leg1
  N23: J1.pin28, S23.leg1
  N24: J1.pin29, S24.leg1
  N25: J1.pin32, S25.leg1
  N26: J1.pin33, S26.leg1
  N27: J1.pin34, S27.leg1
  N28: J1.pin35, S28.leg1
  N29: J1.pin36, S29.leg1
  N30: J1.pin37, S30.leg1
  N31: J1.pin38, S31.leg1
  N32: J1.pin39, S32.leg1

notes:
  Output pins til I2C I/O Interface
  3V3
  InputSimulator
  20240817 1845
  12V
  EXT
  GND
  sekt1953@gmail.com
