# Fritzing sketch OutputSimulator (saved by Fritzing 0.9.6b)
circuit board: 5.97795cm x 1.90445cm
breadboards: 1

parts:
  J1 = female pin header, 4 pins [form="♀ (female)"]
  J2 = female pin header, 4 pins [form="♀ (female)"]
  J3 = female pin header, 4 pins [form="♀ (female)"]
  J4 = female pin header, 4 pins [form="♀ (female)"]
  LED1 = LED - 5mm [color="Red (633nm)" current=0.030 package="5 mm [THT]"]
  LED2 = LED - 5mm [color="Red (633nm)" current=0.030 package="5 mm [THT]"]
  LED3 = LED - 5mm [color="Red (633nm)" current=0.030 package="5 mm [THT]"]
  LED4 = LED - 5mm [color="Red (633nm)" current=0.030 package="5 mm [THT]"]
  LED6 = LED - 5mm [color="Red (633nm)" current=0.030 package="5 mm [THT]"]
  LED7 = LED - 5mm [color="Red (633nm)" current=0.030 package="5 mm [THT]"]
  LED8 = LED - 5mm [color="Red (633nm)" current=0.030 package="5 mm [THT]"]
  LED5 = LED - 5mm [color="Red (633nm)" current=0.030 package="5 mm [THT]"]
  LED10 = LED - 5mm [color="Red (633nm)" current=0.030 package="5 mm [THT]"]
  LED11 = LED - 5mm [color="Red (633nm)" current=0.030 package="5 mm [THT]"]
  LED12 = LED - 5mm [color="Red (633nm)" current=0.030 package="5 mm [THT]"]
  LED13 = LED - 5mm [color="Red (633nm)" current=0.030 package="5 mm [THT]"]
  LED14 = LED - 5mm [color="Red (633nm)" current=0.030 package="5 mm [THT]"]
  LED15 = LED - 5mm [color="Red (633nm)" current=0.030 package="5 mm [THT]"]
  LED16 = LED - 5mm [color="Red (633nm)" current=0.030 package="5 mm [THT]"]
  LED17 = LED - 5mm [color="Red (633nm)" current=0.030 package="5 mm [THT]"]
  3V3 = female pin header, 2 pins [form="♀ (female)"]
  GND = female pin header, 2 pins [form="♀ (female)"]

nets:
  N1: J1.pin1, LED1.anode
  N2: J1.pin2, LED11.anode
  N3: J1.pin3, LED2.anode
  N4: J1.pin4, LED13.anode
  N5: J2.pin1, LED3.anode
  N6: J2.pin2, LED12.anode
  N7: J2.pin3, LED4.anode
  N8: J2.pin4, LED15.anode
  N9: J3.pin1, LED5.cathode
  N10: J3.pin2, LED16.cathode
  N11: J3.pin3, LED6.cathode
  N12: J3.pin4, LED14.cathode
  N13: J4.pin1, LED7.cathode
  N14: J4.pin2, LED17.cathode
  N15: J4.pin3, LED8.cathode
  N16: J4.pin4, LED10.cathode
  N17: LED1.cathode, LED2.cathode, LED3.cathode, LED4.cathode, LED11.cathode, LED12.cathode, LED13.cathode, LED15.cathode, GND.pin1, GND.pin2
  N18: LED6.anode, LED7.anode, LED8.anode, LED5.anode, LED10.anode, LED14.anode, LED16.anode, LED17.anode, 3V3.pin1, 3V3.pin2
