# Fritzing sketch TB6612FNG_04 (saved by Fritzing 0.9.6b)
stripboards: 1

parts:
  Part4 = Motor Driver 1A Dual TB6612FNG  # not connected
  Part5 = Motor Driver 1A Dual TB6612FNG  # not connected
  J10 = male pin header, 2 pins [form="♂ (male)"]
  J11 = male pin header, 2 pins [form="♂ (male)"]
  J12 = male pin header, 4 pins [form="♂ (male)"]
  J13 = male pin header, 2 pins [form="♂ (male)"]
  J14 = male pin header, 2 pins [form="♂ (male)"]
  J15 = male pin header, 4 pins [form="♂ (male)"]
  J19 = female pin header, 8 pins [form="♀ (female)"]
  J20 = female pin header, 8 pins [form="♀ (female)"]
  J18 = female pin header, 8 pins [form="♀ (female)"]
  J17 = female pin header, 8 pins [form="♀ (female)"]
  J16 = male pin header, 4 pins [form="♂ (male)"]

nets:
  N1: J10.pin1, J20.pin5
  N2: J10.pin2, J20.pin6
  N3: J11.pin1, J20.pin2
  N4: J11.pin2, J20.pin3
  N5: J12.pin1, J19.pin4
  N6: J12.pin2, J19.pin5
  N7: J12.pin3, J19.pin6
  N8: J12.pin4, J19.pin7
  N9: J13.pin1, J18.pin5
  N10: J13.pin2, J18.pin6
  N11: J14.pin1, J18.pin2
  N12: J14.pin2, J18.pin3
  N13: J15.pin1, J17.pin4
  N14: J15.pin2, J17.pin5
  N15: J15.pin3, J17.pin6
  N16: J15.pin4, J17.pin7
  N17: J19.pin1, J17.pin1, J16.pin3, J16.pin4
  N18: J19.pin2, J20.pin1, J20.pin4, J20.pin7, J18.pin1, J18.pin4, J18.pin7, J17.pin2, J16.pin1
  N19: J19.pin3, J19.pin8, J20.pin8, J18.pin8, J17.pin3, J17.pin8, J16.pin2

notes:
  Input
  Motor
  3v3
  GND
  12V
  Power In
  Key
  B01
  B02
  A02
  A01
