# Fritzing sketch Currens (saved by Fritzing 0.9.6b)

parts:
  U1 = LM 358 Dual Op-Amp [package="SO 08 [SMD]"]
  R1 = Resistor [tolerance=±5% power=0.25 resistance=220 package=THT]
  R2 = Resistor [tolerance=±5% power=0.25 resistance=220 package=THT]
  R3 = Resistor [tolerance=±5% power=0.25 resistance=220 package=THT]
  R4 = Resistor [tolerance=±5% power=0.25 resistance=220 package=THT]

nets:
  N1: U1.connector2, R4.Pin_1
  N2: U1.connector4, R1.Pin_1, R3.Pin_1, R4.Pin_0
  N3: U1.connector5, R2.Pin_1
  N4: U1.connector6, R1.Pin_0
  GND: R3.Pin_0
