# Fritzing sketch Princip Sketch (saved by Fritzing 0.9.6b)
breadboards: 1

parts:
  U1 = Sharp PC847X [package=THT]
  D1 = Rectifier Diode [part_number=1N4001 package="300 mil [THT]"]
  D2 = Rectifier Diode [part_number=1N4001 package="300 mil [THT]"]
  D3 = Rectifier Diode [part_number=1N4001 package="300 mil [THT]"]
  Track_Power = Screw terminal - 2 pins [package=THT]
  R1 = Resistor [tolerance=±5% power=0.25 resistance=470 package=THT]
  R2 = Resistor [tolerance=±5% power=0.25 resistance=22 package=THT]
  Wagon_short_max = Resistor [tolerance=±5% power=0.25 resistance=2.2k package=THT]
  Track_Section = Screw terminal - 2 pins [package=THT]
  R3 = Resistor [tolerance=±5% power=0.25 resistance=10k package=THT]
  D4 = Rectifier Diode [part_number=1N4001 package="300 mil [THT]"]
  D5 = Rectifier Diode [part_number=1N4001 package="300 mil [THT]"]
  D7 = Rectifier Diode [part_number=1N4001 package="300 mil [THT]"]
  R4 = Resistor [tolerance=±5% power=0.25 resistance=470 package=THT]
  R5 = Resistor [tolerance=±5% power=0.25 resistance=22 package=THT]
  D8 = Rectifier Diode [part_number=1N4001 package="300 mil [THT]"]
  D9 = Rectifier Diode [part_number=1N4001 package="300 mil [THT]"]
  D10 = Rectifier Diode [part_number=1N4001 package="300 mil [THT]"]
  D11 = Rectifier Diode [part_number=1N4001 package="300 mil [THT]"]
  D12 = Rectifier Diode [part_number=1N4001 package="300 mil [THT]"]
  D13 = Rectifier Diode [part_number=1N4001 package="300 mil [THT]"]
  Wagon_short_max1 = Resistor [tolerance=±5% power=0.25 resistance=2.2k package=THT]
  Track_Section1 = Screw terminal - 2 pins [package=THT]
  R6 = Resistor [tolerance=±5% power=0.25 resistance=10k package=THT]
  R7 = Resistor [tolerance=±5% power=0.25 resistance=10k package=THT]
  R8 = Resistor [tolerance=±5% power=0.25 resistance=10k package=THT]
  U3 = PCF8574N [package="DIP16 [THT]"]

nets:
  N1: U1.Pin_1, U1.Pin_3, U1.Pin_5, U1.Pin_7, D1.anode, Track_Power.pin1, R1.Pin_0, D7.cathode, R4.Pin_0, D8.cathode, D9.anode
  N2: U1.Pin_2, R2.Pin_1
  N3: U1.Pin_4, R5.Pin_1
  GND: U1.Pin_9, U1.Pin_11, U1.Pin_13, U1.Pin_15, U3.GND
  N4: U1.Pin_10, R8.Pin_1, U3.P3
  N5: U1.Pin_12, R6.Pin_1, U3.P2
  N6: U1.Pin_14, R7.Pin_1, U3.P1
  N7: U1.Pin_16, R3.Pin_1, U3.P0
  N8: D1.cathode, D2.anode
  N9: D2.cathode, D3.anode
  N10: D3.cathode, R1.Pin_1, R2.Pin_0, Wagon_short_max.Pin_0, Track_Section.pin2, D4.anode
  N11: Track_Power.pin2, Wagon_short_max.Pin_1, Track_Section.pin1, Wagon_short_max1.Pin_1, Track_Section1.pin1
  3.3V: R3.Pin_0, R6.Pin_0, R7.Pin_0, R8.Pin_0, U3.VCC
  N12: D4.cathode, D5.anode
  N13: D5.cathode, D7.anode
  N14: R4.Pin_1, R5.Pin_0, D12.anode, D13.cathode, Wagon_short_max1.Pin_0, Track_Section1.pin2
  N15: D8.anode, D10.cathode
  N16: D9.cathode, D11.anode
  N17: D10.anode, D12.cathode
  N18: D11.cathode, D13.anode

custom parts:
  PCF8574N: 8-bit parallel-load shift registers sekt1953@gmail.com
