# Fritzing sketch Signalprint 2025 (saved by Fritzing 1.0.5)
circuit board: 6.868cm x 3.81436cm
breadboards: 1

parts:
  Part1 = Arduino Nano (Rev3.0)
  IC1 = IC, DIP package, 4 pins [chip_label=IC]
  R1 = Resistor [tolerance=±5% power=0.25 resistance=220 package=THT]
  R2 = Resistor [tolerance=±5% power=0.25 resistance=220 package=THT]
  R3 = Resistor [tolerance=±5% power=0.25 resistance=220 package=THT]
  R4 = Resistor [tolerance=±5% power=0.25 resistance=220 package=THT]
  R5 = Resistor [tolerance=±5% power=0.25 resistance=220 package=THT]
  R6 = Resistor [tolerance=±5% power=0.25 resistance=220 package=THT]
  J1 = female pin header, 7 pins [form="♀ (female)"]
  J2 = female pin header, 5 pins [form="♀ (female)"]
  J3 = female pin header, 5 pins [form="♀ (female)"]
  J4 = female pin header, 4 pins [form="♀ (female)"]
  J5 = female pin header, 2 pins [form="♀ (female)"]
  J6 = female pin header, 2 pins [form="♀ (female)"]

nets:
  Reset: Part1.RESET, J2.pin1, J3.pin1
  N1: Part1.D2, J2.pin4, J3.pin4
  N2: Part1.D3, R6.Pin_1
  N3: Part1.D4, J2.pin5, J3.pin5
  N4: Part1.D5, R5.Pin_1
  N5: Part1.D6, R4.Pin_1
  N6: Part1.D7, J4.pin2
  N7: Part1.D8, J4.pin3
  N8: Part1.D9, R3.Pin_1
  N9: Part1.D10, R2.Pin_1
  N10: Part1.D11/MOSI, R1.Pin_1
  N11: Part1.D12/MISO, J4.pin4
  vcc: Part1.VIN, J1.pin7, J2.pin3, J3.pin3
  Gnd: Part1.GND, J2.pin2, J3.pin2
  N12: Part1.A5, IC1.pin1
  N13: Part1.A4, IC1.pin2
  N14: Part1.D13/SCK, J4.pin1
  SDA: IC1.pin3, J5.pin2, J6.pin2
  SCL: IC1.pin4, J5.pin1, J6.pin1
  N15: R1.Pin_0, J1.pin1
  N16: R2.Pin_0, J1.pin2
  N17: R3.Pin_0, J1.pin3
  N18: R4.Pin_0, J1.pin4
  N19: R5.Pin_0, J1.pin5
  N20: R6.Pin_0, J1.pin6

notes:
  D11
  D10
  D9
  D6
  D5
  D3
  +5V
  D4
  D2
  RST
  GND
  I2C on/off
  SDA
  SCL
  D12
  D7
  D13
  D8
  USB
